# Fritzing sketch ButtonInput_Fritzing_BreadboardView (saved by Fritzing 0.9.3b)
breadboards: 1

parts:
  Part1 = Adafruit Feather M0 WINC1500 [part_number="Adafruit #3010"]
  BUTTON1 = Arcade Button (blue)

nets:
  N1: Part1.+3V3, BUTTON1.no_name_yet#1
  N2: Part1.D11, BUTTON1.no_name_yet#2

custom parts:
  Adafruit Feather M0 WINC1500: This is the Adafruit Feather M0 WiFi w/ATWINC1500 - our take on an 'all-in-one' Arduino-compatible + high speed, reliable WiFi with built in USB and battery charging. Its an Adafruit Feather M0 with a WiFi module, ready to rock! Connect your Feather to the Internet with this fine new FCC-certified WiFi module from Atmel. This 802.11bgn-capable WiFi module is the best new thing for networking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
  Arcade Button (blue): Adafruit Arcade Button (blue)
